# Fritzing sketch BigSound (saved by Fritzing 0.9.0b)

parts:
  pyboard_v1_1 = PyBoard v1.0
  BuzzerDFR1 = BuzzerDFR0032
  VCC3 = Battery
  VCC2 = Battery

nets:
  N1: pyboard_v1_1.X1, BuzzerDFR1.Signal
  N2: pyboard_v1_1.GND#53, BuzzerDFR1.GND
  N3: pyboard_v1_1.GND#55, VCC3.-
  N4: pyboard_v1_1.VIN, VCC2.+
  N5: VCC3.+, VCC2.-
