# Fritzing sketch Geraldo (saved by Fritzing 0.9.0b)
breadboards: 1

parts:
  VCC2 = Battery
  J1 = Infrared Proximity Sensor
  J2 = Basic Servo
  J3 = Basic Servo
  pyboard_v1_1 = PyBoard v1.0
  LED1 = RGB LED - (4 legs) [package="5 mm [THT]"]
  VCC1 = Battery

nets:
  N1: VCC2.-, J1.GND, pyboard_v1_1.GND#55
  N2: VCC2.+, VCC1.-
  N3: J1.Vout, pyboard_v1_1.X5
  N4: J1.Vcc, pyboard_v1_1.VIN#57, VCC1.+
  N5: J2.gnd, pyboard_v1_1.GND#52
  N6: J2.vcc, pyboard_v1_1.VIN#43
  N7: J2.pulse, pyboard_v1_1.X1
  N8: J3.gnd, pyboard_v1_1.GND#58
  N9: J3.vcc, pyboard_v1_1.VIN#59
  N10: J3.pulse, pyboard_v1_1.X2
  N11: pyboard_v1_1.Y4, LED1.blue_cathode
  N12: pyboard_v1_1.Y6, LED1.red_cathode
  N13: pyboard_v1_1.GND#62, LED1.common_anode
